// Logisim project cpu.circ as structural Verilog: 1 circuit, main circuit cpu
module cpu (
  input  clk,
  input  [31:0] Instruction,
  input  [31:0] MemReadData,
  output [31:0] MemAddress,
  output [31:0] ProgramCounter,
  output [31:0] ra,
  output [31:0] sp,
  output [31:0] t0,
  output [31:0] t1,
  output [31:0] t2,
  output [31:0] s0,
  output [31:0] s1,
  output [31:0] a0,
  output [3:0] MemWriteMask,
  output [31:0] MemWriteData
);

  wire ASel, BrEq, BrLt, BrUn, BSel, MemWEn, PCSel, RegWEn;
  wire [1:0] WBSel;
  wire [2:0] ImmSel;
  wire [3:0] ALUSel;
  wire [31:0] adder_1_out, adder_2_out, DEMEResult, imm, InstructionToStage2, multiplexer_1_out,
       multiplexer_2_out, multiplexer_4_out, multiplexer_5_out, PC_q, ReadData1, ReadData2, register_1_q;

  Adder #(.width(32)) adder_1 (.a(PC_q), .b(32'h4), .out(adder_1_out));  // open: cin, cout
  Multiplexer #(.width(32)) multiplexer_1 (.in0(adder_1_out), .in1(MemAddress), .out(multiplexer_1_out), .sel(PCSel));
  Register #(.width(32)) PC (.D(multiplexer_1_out), .clk(clk), .Q(PC_q));  // open: en, clr
  Register #(.width(32)) register_1 (.D(Instruction), .clk(clk), .Q(register_1_q));  // open: en, clr
  Adder #(.width(32)) adder_2 (.a(ProgramCounter), .b(32'h4), .out(adder_2_out));  // open: cin, cout
  Register #(.width(32)) register_2 (.D(PC_q), .clk(clk), .Q(ProgramCounter));  // open: en, clr
  Multiplexer #(.select(2), .width(32)) multiplexer_2 (
    .in0({32{1'b1}}), .in1(MemAddress), .in2(DEMEResult), .in3(adder_2_out), .out(multiplexer_2_out),
    .sel(WBSel));
  Multiplexer #(.width(32)) multiplexer_3 (.in0(register_1_q), .in1(32'h13), .out(InstructionToStage2), .sel(PCSel));
  control_logic control_logic_1 (
    .Instruction(InstructionToStage2), .BrEq(BrEq), .BrLt(BrLt), .PCSel(PCSel), .RegWEn(RegWEn),
    .ImmSel(ImmSel), .BrUn(BrUn), .ASel(ASel), .BSel(BSel), .ALUSel(ALUSel), .MemWEn(MemWEn), .WBSel(WBSel));
  regfile regfile_1 (
    .ReadIndex1(InstructionToStage2[19:15]), .ReadIndex2(InstructionToStage2[24:20]),
    .WriteIndex(InstructionToStage2[11:7]), .WriteData(multiplexer_2_out), .RegWEn(RegWEn), .clk(clk),
    .ra(ra), .sp(sp), .t0(t0), .t1(t1), .t2(t2), .s0(s0), .s1(s1), .a0(a0), .ReadData1(ReadData1),
    .ReadData2(ReadData2));
  imm_gen imm_gen_1 (.Instruction(InstructionToStage2), .ImmSel(ImmSel), .Immediate(imm));
  Multiplexer #(.width(32)) multiplexer_4 (.in0(ReadData1), .in1(ProgramCounter), .out(multiplexer_4_out), .sel(ASel));
  Multiplexer #(.width(32)) multiplexer_5 (.in0(ReadData2), .in1(imm), .out(multiplexer_5_out), .sel(BSel));
  alu alu_1 (.A(multiplexer_4_out), .B(multiplexer_5_out), .ALUSel(ALUSel), .ALUResult(MemAddress));
  branch_comp branch_comp_1 (.BrData1(ReadData1), .BrData2(ReadData2), .BrUn(BrUn), .BrEq(BrEq), .BrLt(BrLt));
  partial_store partial_store_1 (
    .Instruction(InstructionToStage2), .MemAddress(MemAddress), .DataFromReg(ReadData2), .MemRW(MemWEn),
    .MemWriteMask(MemWriteMask), .DataToMem(MemWriteData));
  partial_load partial_load_1 (
    .Instruction(InstructionToStage2), .MemAddress(MemAddress), .DataFromMem(MemReadData),
    .DataToReg(DEMEResult));

  // Other names for the same wires on the sheet: ALUResult[31:0] = MemAddress

  // Notes on the sheet:
  //   To IMEM
  //   IMEM (do **NOT** move this)
  //   From IMEM
  //   Inputs/Outputs for testing. Do **NOT** move these.
  //   It is OK to move the PC, RegFile, ALU, MEM, Branch Comp, Imm Gen, Partial Load, Partial Store and Control Logic to wherever is most convenient for you when constructing your CPU, and to delete this text
  //   To DMEM
  //   DMEM (do **NOT** move this)
  //   From DMEM
endmodule
